# Fritzing sketch MotorsWithController (saved by Fritzing 0.9.3b)
breadboards: 1

parts:
  Raspberry_Pi_1 = Raspberry Pi 3 [part_number=RPI-3-V1.2]
  VCC1 = 4 x AAA Battery Mount
  J1 = Basic Servo
  J2 = Basic Servo
  S1 = Round Pushbutton
  S2 = Round Pushbutton
  S3 = Round Pushbutton
  S4 = Round Pushbutton
  S5 = Round Pushbutton
  S6 = Round Pushbutton
  S7 = H-Bridge with L298N
  JP1 = Header 5x2 [package=2x5-raf]
  R1 = Resistor [tolerance=±5% resistance=220 package="0805 [SMD]"]
  R2 = Resistor [tolerance=±5% resistance=220 package="0805 [SMD]"]
  R3 = Resistor [tolerance=±5% resistance=220 package="0805 [SMD]"]
  R4 = Resistor [tolerance=±5% resistance=220 package="0805 [SMD]"]
  R5 = Resistor [tolerance=±5% resistance=220 package="0805 [SMD]"]
  R6 = Resistor [tolerance=±5% resistance=220 package="0805 [SMD]"]
  J3 = Basic Servo

nets:
  N1: Raspberry_Pi_1.GIPO17, S3.leg0, R1.Pin_1
  N2: Raspberry_Pi_1.GIPO27, S4.leg0, R2.Pin_1
  N3: Raspberry_Pi_1.GIPO22, S1.leg0, R4.Pin_1
  N4: Raspberry_Pi_1.GIPO5, S7.IN1
  N5: Raspberry_Pi_1.GIPO6, S7.IN2
  N6: Raspberry_Pi_1.GIPO19, S7.IN4
  GND: Raspberry_Pi_1.GND, VCC1.-, J1.gnd, J2.gnd, S1.leg1, S2.leg1, S3.leg1, S4.leg1, S5.leg1, S6.leg1, S7.GND, JP1.9, J3.gnd
  N7: Raspberry_Pi_1.GIPO21, S6.leg0, R6.Pin_1
  N8: Raspberry_Pi_1.GIPO20, S5.leg0, R5.Pin_1
  N9: Raspberry_Pi_1.GIPO16, S2.leg0, R3.Pin_1
  N10: Raspberry_Pi_1.5V, JP1.1, R1.Pin_0, R2.Pin_0, R3.Pin_0, R4.Pin_0, R5.Pin_0, R6.Pin_0
  N11: VCC1.+, J2.vcc
  N12: J1.pulse, S7.M1-02
  N13: J2.pulse, S7.M2-02
  12V: S7.12V, J3.vcc
  N14: S7.M1-01, J3.pulse

custom parts:
  H-Bridge with L298N: h-bridge
